# Fritzing sketch Circuito control de temperatura (saved by Fritzing 1.0.4)

parts:
  M1 = DOIT Esp32 DevKit v1 (30 pins long, 11 pins width) [part_number=ESP32S-PIN30]
  Mod1 = KY-019 5V Relay Module [package="Breakout board"]
  F1 = Fan - Ventilador [package=THT]
  Boost_Convertor1 = Boost Convertor [part_number=XL6009E1 package=THT]
  DHT1 = DHT11 Humitidy and Temperature Sensor (3 pins)

nets:
  N1: M1.3V3, Mod1.+, DHT1.Plus
  GND: M1.GND, Mod1.-, Boost_Convertor1.Negative_Input, DHT1.Gnd
  N2: M1.D4, DHT1.Signal
  N3: M1.D27, Mod1.S
  N4: M1.VIN, Boost_Convertor1.Positive_Input
  N5: Mod1.NC, F1.5V, Boost_Convertor1.Negative_Output
  N6: Mod1.Common, F1.GND, Boost_Convertor1.Positive_Output

custom parts:
  DOIT Esp32 DevKit v1 (30 pins long, 11 pins width): The DOIT Esp32 DevKit v1 is one of the development board created by DOIT to evaluate the ESP-WROOM-32 module. It is based on the ESP32 microcontroller that boasts Wifi, Bluetooth, Ethernet and Low Power support all in a single chip. (vanepp) made breadboard work, adjusted pin numbering and labels and reduced size of schematic and cleaned up pcb. This chip is 30pins long (2 x15) and 11 pins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
  KY-019 5V Relay Module: KY-019 5V Relay module, used to control AC circuits. (Special thanks to vanepp for fixing the PCB holes and other errors)
  Fan - Ventilador: Ventilador de 2 pines, se encuentra comunmente en computadoras de escritorio
  Boost Convertor: DC to DC boost convertor
  DHT11 Humitidy and Temperature Sensor (3 pins): DHT11 Humidity and Temperature Sensor (3 pins).
