# Fritzing sketch Circuito de encendido y apagado (Luz) (saved by Fritzing 1.0.4)

parts:
  M1 = DOIT Esp32 DevKit v1 (30 pins long, 11 pins width) [part_number=ESP32S-PIN30]
  Mod1 = KY-019 5V Relay Module [package="Breakout board"]
  LED1 = LEDs [package=led10mm]
  M2 = CK-07 [package=THT]
  R1 = Photocell (LDR) [power=0.25W dark_resistance_@0.01lx=300kΩ light_resistance_@100lx=400Ω luminance=10lx package=THT]

nets:
  N1: M1.3V3, Mod1.+, M2.pin_4
  N2: M1.GND, Mod1.-, M2.pin_3
  N3: M1.D22, M2.pin_2
  N4: M1.D25, Mod1.S
  N5: Mod1.Common, LED1.A
  N6: Mod1.NO, LED1.C
  N7: M2.pin_5, R1.pin_0
  N8: M2.pin_6, R1.pin_1

custom parts:
  DOIT Esp32 DevKit v1 (30 pins long, 11 pins width): The DOIT Esp32 DevKit v1 is one of the development board created by DOIT to evaluate the ESP-WROOM-32 module. It is based on the ESP32 microcontroller that boasts Wifi, Bluetooth, Ethernet and Low Power support all in a single chip. (vanepp) made breadboard work, adjusted pin numbering and labels and reduced size of schematic and cleaned up pcb. This chip is 30pins long (2 x15) and 11 pins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
  KY-019 5V Relay Module: KY-019 5V Relay module, used to control AC circuits. (Special thanks to vanepp for fixing the PCB holes and other errors)
  LEDs: LEDs Standard schematic elements and footprints for 5mm, 3mm, 1206, and 0603 sized LEDs. 5mm - Spark Fun Electronics SKU : COM-00529 (and others)
  CK-07: Fc-51 Infrared Obstacle Avoidance Proximity Sensor module. IR transmitter led, receiver LED, lm393 compaitor and a pot. 3.3 V to 5V power.
