# Fritzing sketch Circuito de energia (saved by Fritzing 1.0.4)
# 18650 Li-ion Battery: CC-BY Dr Kristofer Chan, King's College London/Remote-research.org

parts:
  MH-CD1 = MH-CD42
  M1 = DOIT Esp32 DevKit v1 (30 pins long, 11 pins width) [part_number=ESP32S-PIN30]
  BAT1 = 18650 Li-ion Battery [package=battery-18650]
  J1 = Power Jack [package=power_jack_combo]

nets:
  N1: MH-CD1.OUT_+5V, M1.VIN
  N2: MH-CD1.GND#2, M1.GND
  N3: MH-CD1.BAT, BAT1.+
  N4: MH-CD1.GND#4, BAT1.-
  N5: MH-CD1.GND#5, J1.GND, J1.GNDBREAK
  N6: MH-CD1.VIN, J1.PWR

custom parts:
  MH-CD42: The MH-CD42 is a compact module designed for use with a single (1S) Li-Ion or Li-Po cell, or multiple cells connected in parallel. At its core, the module uses the IP5306 power management chip, a robust solution for efficient power regulation both for charging and for discharging. This 16x25mm module integrates all necessary components for building power banks, portable chargers, or adding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
  DOIT Esp32 DevKit v1 (30 pins long, 11 pins width): The DOIT Esp32 DevKit v1 is one of the development board created by DOIT to evaluate the ESP-WROOM-32 module. It is based on the ESP32 microcontroller that boasts Wifi, Bluetooth, Ethernet and Low Power support all in a single chip. (vanepp) made breadboard work, adjusted pin numbering and labels and reduced size of schematic and cleaned up pcb. This chip is 30pins long (2 x15) and 11 pins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
  18650 Li-ion Battery: 18650 li-ion Battery Standard 18650 battery with interactive connectors Creative Common Attribution 4.0 International (CC-BY 4.0) license. Any use of this part requires attribution of Dr Kristofer Chan, Department of Geography, King's College London. Contact kristofer.chan [at] kcl.ac.uk OR kris [at] remote-research.org for further information.
