# Fritzing sketch Circuito medicion nivel de agua (saved by Fritzing 1.0.4)

parts:
  M1 = DOIT Esp32 DevKit v1 (30 pins long, 11 pins width) [part_number=ESP32S-PIN30]
  Water_Level_Sensor1 = Water Level Sensor
  Part1 = KY-006 Passive Buzzer Module [package="Breakout board"]

nets:
  3V3: M1.3V3, Water_Level_Sensor1.VCC
  GND: M1.GND, Water_Level_Sensor1.GND, Part1.-
  N1: M1.D18, Part1.S
  N2: M1.D35, Water_Level_Sensor1.SIG

custom parts:
  DOIT Esp32 DevKit v1 (30 pins long, 11 pins width): The DOIT Esp32 DevKit v1 is one of the development board created by DOIT to evaluate the ESP-WROOM-32 module. It is based on the ESP32 microcontroller that boasts Wifi, Bluetooth, Ethernet and Low Power support all in a single chip. (vanepp) made breadboard work, adjusted pin numbering and labels and reduced size of schematic and cleaned up pcb. This chip is 30pins long (2 x15) and 11 pins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
  Water Level Sensor: A water level sensor. This sensor operates at 3V to 5V. The Sig (signal) pin outputs an analogue signal that is in proportion to the amount of water in contact with the sensor.
  KY-006 Passive Buzzer Module: Passive Piezoelectric Buzzer Module Keyes KY-006, it can produce a range of sound tones depending on the input frequency.
