# Fritzing sketch Circuito Riego Automático (saved by Fritzing 1.0.4)

parts:
  M1 = DOIT Esp32 DevKit v1 (30 pins long, 11 pins width) [part_number=ESP32S-PIN30]
  Componente1 = FC-28 Soil Hygrometer Module - Probe
  Componente2 = FC-28 Soil Hygrometer Module
  Mod1 = KY-019 5V Relay Module [package="Breakout board"]
  WATER_PUMP1 = water pump/motor  # not connected

nets:
  3V3: M1.3V3, Componente2.VCC, Mod1.+
  GND: M1.GND, Componente2.GND, Mod1.-
  N1: M1.D23, Mod1.S
  N2: M1.D34, Componente2.AO
  N3: Componente1.POS, Componente2.POS
  N4: Componente1.NEG, Componente2.NEG

custom parts:
  DOIT Esp32 DevKit v1 (30 pins long, 11 pins width): The DOIT Esp32 DevKit v1 is one of the development board created by DOIT to evaluate the ESP-WROOM-32 module. It is based on the ESP32 microcontroller that boasts Wifi, Bluetooth, Ethernet and Low Power support all in a single chip. (vanepp) made breadboard work, adjusted pin numbering and labels and reduced size of schematic and cleaned up pcb. This chip is 30pins long (2 x15) and 11 pins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
  FC-28 Soil Hygrometer Module - Probe: The FC-28 is a soil hygrometer module that uses the Texas Instruments LM393 comparator chip to provide an analog measurement of soil humidity.
  FC-28 Soil Hygrometer Module: The FC-28 is a soil hygrometer module that uses the Texas Instruments LM393 comparator chip to provide an analog measurement of soil humidity. The digital output is high when soil moisture is over a certain threshold, as determined by adjusting the potentiometer.
  KY-019 5V Relay Module: KY-019 5V Relay module, used to control AC circuits. (Special thanks to vanepp for fixing the PCB holes and other errors)
  water pump/motor: WATER PUMP BY ARDUBLOCKTR
